// Digital circuit decoder.dig as structural Verilog
module decoder (
  input  [31:0] instr,
  output [1:0] out_2,
  output [1:0] out_3,
  output [1:0] out_4,
  output [1:0] out_5,
  output [1:0] out_6,
  output [1:0] out_7,
  output [1:0] out_8,
  output [1:0] out_9
);

  Demultiplexer #(.Bits(2), .Selector_Bits(3)) demultiplexer_1 (
    .sel(instr[4:2]), .in(instr[6:5]), .out_0(out_2), .out_1(out_3), .out_2(out_4), .out_3(out_5),
    .out_4(out_6), .out_5(out_7), .out_6(out_8), .out_7(out_9));

  // Notes on the sheet:
  //   instr: default 51
  //   OpCode
  //   [1,0] = 11, always
  //   LOAD, STORE, MADD, BRANCH
  //   LOAD-FP, STORE-FP, MSUB, JALR
  //   cust, cust, NMSUB, reserved
  //   MISC-MEM, AMO, NMADD, JAL
  //   OP-IMM, OP, OP-FP, SYSTEM
  //   AUIPC, LUI, reserved, reserved
  //   OP-IMM-32, OP-32, cust, cust
  //   instruction > 32-bits
endmodule
