// Digital circuit i_type_decoder.dig as structural Verilog
module i_type_decoder (
  input  [31:0] instr,
  output [4:0] rd,
  output [4:0] rs1,
  output [11:0] imm12
);


  assign imm12 = instr[31:20];
  assign rd = instr[11:7];
  assign rs1 = instr[19:15];
endmodule
