// Digital circuit register_file.dig as structural Verilog
// Register file with 32 32-bit registers
module register_file (
  input  [4:0] rs1,
  input  [4:0] rs2,
  input  [4:0] rd,
  input  [31:0] D_in,
  input  clock,
  output [31:0] D_rs1,
  output [31:0] D_rs2
);

  wire en_x0, en_x1, en_x2, en_x3, en_x4, en_x5, en_x6, en_x7, en_x8, en_x9, en_x10, en_x11, en_x12, en_x13,
       en_x14, en_x15, en_x16, en_x17, en_x18, en_x19, en_x20, en_x21, en_x22, en_x23, en_x24, en_x25,
       en_x26, en_x27, en_x28, en_x29, en_x30, en_x31;
  wire [31:0] D_x0, D_x1, D_x2, D_x3, D_x4, D_x5, D_x6, D_x7, D_x8, D_x9, D_x10, D_x11, D_x12, D_x13, D_x14,
       D_x15, D_x16, D_x17, D_x18, D_x19, D_x20, D_x21, D_x22, D_x23, D_x24, D_x25, D_x26, D_x27, D_x28,
       D_x29, D_x30, D_x31, nor_1_out, x0, x1, x2, x3, x4, x5, x6, x7, x8, x9, x10, x11, x12, x13, x14, x15,
       x16, x17, x18, x19, x20, x21, x22, x23, x24, x25, x26, x27, x28, x29, x30, x31;

  Demultiplexer #(.Selector_Bits(5), .Bits(32)) demultiplexer_1 (
    .sel(rd), .in(D_in), .out_0(D_x0), .out_1(D_x1), .out_2(D_x2), .out_3(D_x3), .out_4(D_x4), .out_5(D_x5),
    .out_6(D_x6), .out_7(D_x7), .out_8(D_x8), .out_9(D_x9), .out_10(D_x10), .out_11(D_x11), .out_12(D_x12),
    .out_13(D_x13), .out_14(D_x14), .out_15(D_x15), .out_16(D_x16), .out_17(D_x17), .out_18(D_x18),
    .out_19(D_x19), .out_20(D_x20), .out_21(D_x21), .out_22(D_x22), .out_23(D_x23), .out_24(D_x24),
    .out_25(D_x25), .out_26(D_x26), .out_27(D_x27), .out_28(D_x28), .out_29(D_x29), .out_30(D_x30),
    .out_31(D_x31));
  Demultiplexer #(.Selector_Bits(5)) demultiplexer_2 (
    .sel(rd), .in(1'b1), .out_0(en_x0), .out_1(en_x1), .out_2(en_x2), .out_3(en_x3), .out_4(en_x4),
    .out_5(en_x5), .out_6(en_x6), .out_7(en_x7), .out_8(en_x8), .out_9(en_x9), .out_10(en_x10),
    .out_11(en_x11), .out_12(en_x12), .out_13(en_x13), .out_14(en_x14), .out_15(en_x15), .out_16(en_x16),
    .out_17(en_x17), .out_18(en_x18), .out_19(en_x19), .out_20(en_x20), .out_21(en_x21), .out_22(en_x22),
    .out_23(en_x23), .out_24(en_x24), .out_25(en_x25), .out_26(en_x26), .out_27(en_x27), .out_28(en_x28),
    .out_29(en_x29), .out_30(en_x30), .out_31(en_x31));
  assign nor_1_out = ~({32{1'b1}} | D_x0);  // NOr nor_1, 32 bits wide
  // register register_1: pin names not known; wires that end beside it: nor_1_out, clock, en_x0, x0
  // register register_2: pin names not known; wires that end beside it: D_x1, clock, en_x1, x1
  // register register_3: pin names not known; wires that end beside it: D_x2, clock, en_x2, x2
  // register register_4: pin names not known; wires that end beside it: D_x3, clock, en_x3, x3
  // register register_5: pin names not known; wires that end beside it: D_x4, clock, en_x4, x4
  // register register_6: pin names not known; wires that end beside it: D_x5, clock, en_x5, x5
  // register register_7: pin names not known; wires that end beside it: D_x6, clock, en_x6, x6
  // register register_8: pin names not known; wires that end beside it: D_x7, clock, en_x7, x7
  // register register_9: pin names not known; wires that end beside it: D_x8, clock, en_x8, x8
  // register register_10: pin names not known; wires that end beside it: D_x9, clock, en_x9, x9
  // register register_11: pin names not known; wires that end beside it: D_x10, clock, en_x10, x10
  // register register_12: pin names not known; wires that end beside it: D_x11, clock, en_x11, x11
  // register register_13: pin names not known; wires that end beside it: D_x12, clock, en_x12, x12
  // register register_14: pin names not known; wires that end beside it: D_x13, clock, en_x13, x13
  // register register_15: pin names not known; wires that end beside it: D_x14, clock, en_x14, x14
  // register register_16: pin names not known; wires that end beside it: D_x15, clock, en_x15, x15
  // register register_17: pin names not known; wires that end beside it: D_x16, clock, en_x16, x16
  // register register_18: pin names not known; wires that end beside it: D_x17, clock, en_x17, x17
  // register register_19: pin names not known; wires that end beside it: D_x18, clock, en_x18, x18
  // register register_20: pin names not known; wires that end beside it: D_x19, clock, en_x19, x19
  // register register_21: pin names not known; wires that end beside it: D_x20, clock, en_x20, x20
  // register register_22: pin names not known; wires that end beside it: D_x21, clock, en_x21, x21
  // register register_23: pin names not known; wires that end beside it: D_x22, clock, en_x22, x22
  // register register_24: pin names not known; wires that end beside it: D_x23, clock, en_x23, x23
  // register register_25: pin names not known; wires that end beside it: D_x24, clock, en_x24, x24
  // register register_26: pin names not known; wires that end beside it: D_x25, clock, en_x25, x25
  // register register_27: pin names not known; wires that end beside it: D_x26, clock, en_x26, x26
  // register register_28: pin names not known; wires that end beside it: D_x27, clock, en_x27, x27
  // register register_29: pin names not known; wires that end beside it: D_x28, clock, en_x28, x28
  // register register_30: pin names not known; wires that end beside it: D_x29, clock, en_x29, x29
  // register register_31: pin names not known; wires that end beside it: D_x30, clock, en_x30, x30
  // register register_32: pin names not known; wires that end beside it: D_x31, clock, en_x31, x31
  Multiplexer #(.Selector_Bits(5), .Bits(32)) multiplexer_1 (
    .sel(rs2), .in_0(x0), .in_1(x1), .in_2(x2), .in_3(x3), .in_4(x4), .in_5(x5), .in_6(x6), .in_7(x7),
    .in_8(x8), .in_9(x9), .in_10(x10), .in_11(x11), .in_12(x12), .in_13(x13), .in_14(x14), .in_15(x15),
    .in_16(x16), .in_17(x17), .in_18(x18), .in_19(x19), .in_20(x20), .in_21(x21), .in_22(x22), .in_23(x23),
    .in_24(x24), .in_25(x25), .in_26(x26), .in_27(x27), .in_28(x28), .in_29(x29), .in_30(x30), .in_31(x31),
    .out(D_rs2));
  Multiplexer #(.Selector_Bits(5), .Bits(32)) multiplexer_2 (
    .sel(rs1), .in_0(x0), .in_1(x1), .in_2(x2), .in_3(x3), .in_4(x4), .in_5(x5), .in_6(x6), .in_7(x7),
    .in_8(x8), .in_9(x9), .in_10(x10), .in_11(x11), .in_12(x12), .in_13(x13), .in_14(x14), .in_15(x15),
    .in_16(x16), .in_17(x17), .in_18(x18), .in_19(x19), .in_20(x20), .in_21(x21), .in_22(x22), .in_23(x23),
    .in_24(x24), .in_25(x25), .in_26(x26), .in_27(x27), .in_28(x28), .in_29(x29), .in_30(x30), .in_31(x31),
    .out(D_rs1));

  // Notes on the sheet:
  //   D_rs1: This outputs the 32-bit data stored at the register specified by rs2
  //   D_in: 32-bit input to be stored at rd
  //   D_rs2: This outputs the 32-bit data stored at the register specified by rs2
endmodule

/* Test case Register IO:
		clock	rd	D_in 		rs1	D_rs1		rs2	D_rs2
		C	0	0x77 		0	0		0	0
repeat(31)	C     	(n+1) 	(0x7<<n) 	(n+1)	(0x7<<n) 	(n+1)	(0x7<<n)
*/
