// Digital circuit soc.dig as structural Verilog
module soc (
  input  [15:0] value,
  input  [1:0] dest,
  input  [1:0] src,
  input  R_R,
  output [1:0] rs,
  output [15:0] L,
  output [15:0] R,
  output [1:0] rd,
  output [3:0] pc,
  output [15:0] L_2,
  output [31:0] L_rs,
  output [31:0] R_rd,
  output [15:0] out_13
);

  wire add, add_out, advance_out, asm_1_store_clk, jmp, jmp_out, mode_out, pmshim_1_c, pmshim_1_ld,
       pmshim_1_str;
  wire [3:0] pmshim_1_a;
  wire [31:0] asm_1_inst, fetch16_1_d_inst, pmshim_1_d_in, Program_d;

  Button u_add (.out(add_out));
  Button u_jmp (.out(jmp_out));
  LED programming (.in(mode_out));
  DipSwitch mode (.out(mode_out));
  asm asm_1 (
    .mode(mode_out), .imm(value), .dest(dest), .src(src), .add(add_out), .jump(jmp_out), .move(R_R),
    .store_clk(asm_1_store_clk), .inst(asm_1_inst));  // open: R_R
  pmshim pmshim_1 (
    .pc(pc), .S_C(asm_1_store_clk), .inst(asm_1_inst), .A(pmshim_1_a), .D_in(pmshim_1_d_in),
    .str(pmshim_1_str), .C(pmshim_1_c), .ld(pmshim_1_ld));
  EEPROMDualPort #(.AddrBits(4), .Bits(32)) Program (
    .A(pmshim_1_a), .Din(pmshim_1_d_in), .str(pmshim_1_str), .C(pmshim_1_c), .ld(pmshim_1_ld), .D(Program_d));
  Button advance (.out(advance_out));
  fetch16 fetch16_1 (
    .mode(mode_out), .D_stored(Program_d), .D_bypass(asm_1_inst), .C(advance_out), .value(L), .jump(jmp),
    .pc(pc), .D_inst(fetch16_1_d_inst));
  LED add_2 (.in(add));
  LED jump (.in(jmp));
  // decoder decoder_1: pin names not known; wires that end beside it: fetch16_1_d_inst, L_rs, R_rd, rs, rd, L, R, add, jmp
  execute execute_1 (.L(L), .R(R), .add(add), .sum(out_13));
  // register_file register_file_1: pin names not known; wires that end beside it: rd, rs, rd, out_13, advance_out, L_rs, R_rd

  assign L_2 = L;

  // Notes on the sheet:
  //   contents of Program (hex, n*v repeats v):
  //   1,110001,8120000,8020000,8230000,8130000,8320000,8230000,7230006
endmodule
