// Digital circuit asm.dig as structural Verilog
module asm (
  input  mode,
  input  [15:0] imm,
  input  [1:0] dest,
  input  [1:0] src,
  input  add,
  input  jump,
  output [31:0] inst,
  output store_clk
);

  wire priorityencoder_1_any;

  PriorityEncoder #(.Selector_Bits(3)) priorityencoder_1 (
    .in0(add), .in1(1'b0), .in2(1'b0), .in3(1'b0), .in4(1'b0), .in5(1'b0), .in6(1'b0), .in7(jump),
    .num(inst[26:24]), .any(priorityencoder_1_any));
  and and_1 (store_clk, priorityencoder_1_any, mode);

  assign {inst[31:27], inst[23:0]} = {{7{1'b0}}, src, 2'b00, dest, imm};

  // Notes on the sheet:
  //   mode: default 1
  //   imm: default 100
  //   dest: default 1
  //   src: default 1
  //   add: default 100
endmodule
