// Digital circuit decoder16.dig as structural Verilog
module decoder16 (
  input  [31:0] D_inst,
  input  [15:0] L_in,
  input  [15:0] R_in,
  output [1:0] rs,
  output [1:0] rd,
  output [15:0] L_out,
  output [15:0] R_out,
  output [1:0] mux_out,
  output add,
  output jump,
  output move,
  output [2:0] op,
  output R_R
);

  Multiplexer #(.Bits(16)) multiplexer_1 (.sel(D_inst[27]), .in_0(D_inst[15:0]), .in_1(R_in), .out(R_out));
  Decoder #(.Selector_Bits(3)) decoder_1 (
    .sel(D_inst[26:24]), .out_0(add), .out_6(move), .out_7(jump));  // open: out_1, out_2, out_3, out_4, out_5
  PriorityEncoder #(.Selector_Bits(2)) priorityencoder_1 (
    .in0(jump), .in1(add), .in2(move), .in3(1'b0), .num(mux_out));  // open: any

  assign L_out = L_in;
  assign op = D_inst[26:24];
  assign R_R = D_inst[27];
  assign rd = D_inst[17:16];
  assign rs = D_inst[21:20];

  // Notes on the sheet:
  //   D_inst: Take 32-bits input
endmodule
