// Digital circuit fetch16.dig as structural Verilog
module fetch16 (
  input  [15:0] instr,
  input  C,
  input  [15:0] value,
  input  jump,
  output [3:0] pc,
  output [15:0] D_instr
);

  CounterPreset #(.Bits(4)) u_PC (
    .en(1'b1), .C(C), .dir(1'b0), .in(value[3:0]), .ld(jump), .clr(1'b0), .out(pc));  // open: ovf

  assign D_instr = instr;

  // Notes on the sheet:
  //   instr: Take 32-bits input
endmodule
