// Digital circuit front.dig as structural Verilog
module front (
  output [15:0] R0,
  output [15:0] R1,
  output [15:0] R2,
  output [15:0] R3,
  output [3:0] pc,
  output [15:0] L_rs,
  output [15:0] R_rd,
  output [15:0] L_decimal,
  output [15:0] R_decimal
);

  wire add, advance_out, hexdisplay_1_p1, hexdisplay_1_p2, hexdisplay_1_p3, hexdisplay_1_p4, hexdisplay_1_p5,
       hexdisplay_1_p6, hexdisplay_1_p7, hexdisplay_1_p8, hexdisplay_2_p1, hexdisplay_2_p2, hexdisplay_2_p3,
       hexdisplay_2_p4, hexdisplay_2_p5, hexdisplay_2_p6, hexdisplay_2_p7, hexdisplay_2_p8, instdisplay_1_p1,
       instdisplay_1_p2, instdisplay_1_p3, instdisplay_1_p4, instdisplay_1_p5, instdisplay_1_p6, jmp, move,
       pmshim_1_c, pmshim_1_ld, pmshim_1_str, r_r, regdisplay_1_p1, regdisplay_1_p2, regdisplay_2_p1,
       regdisplay_2_p2;
  wire [1:0] decoder16_1_mux_out, rd, rs;
  wire [2:0] op;
  wire [3:0] hexdisplay_1_d1, hexdisplay_1_d2, hexdisplay_1_d3, hexdisplay_1_d4, hexdisplay_1_d5,
       hexdisplay_1_d6, hexdisplay_1_d7, hexdisplay_1_d8, hexdisplay_2_d1, hexdisplay_2_d2, hexdisplay_2_d3,
       hexdisplay_2_d4, hexdisplay_2_d5, hexdisplay_2_d6, hexdisplay_2_d7, hexdisplay_2_d8, pmshim_1_a;
  wire [15:0] exec16_1_sum, fetch16_1_d_instr, instdisplay_1_d1, instdisplay_1_d2, instdisplay_1_d3,
       instdisplay_1_d4, instdisplay_1_d5, instdisplay_1_d6, pmshim_1_d_in, Program_d, regdisplay_1_d1,
       regdisplay_1_d2, regdisplay_2_d1, regdisplay_2_d2;

  SixteenSeg sixteenseg_1 (.led(regdisplay_1_d1), .dp(regdisplay_1_p1));
  regdisplay regdisplay_1 (
    .D1(regdisplay_1_d1), .P1(regdisplay_1_p1), .D2(regdisplay_1_d2), .P2(regdisplay_1_p2), .E(1'b1),
    .J(jmp), .R(rd));
  pmshim pmshim_1 (.pc(pc), .A(pmshim_1_a), .D_in(pmshim_1_d_in), .str(pmshim_1_str), .C(pmshim_1_c), .ld(pmshim_1_ld));
  SixteenSeg sixteenseg_2 (.led(regdisplay_1_d2), .dp(regdisplay_1_p2));
  EEPROMDualPort #(.AddrBits(4), .isProgramMemory("true"), .Bits(16)) Program (
    .A(pmshim_1_a), .Din(pmshim_1_d_in), .str(pmshim_1_str), .C(pmshim_1_c), .ld(pmshim_1_ld), .D(Program_d));
  Button advance (.out(advance_out));
  Seven_Seg_Hex seven_seg_hex_1 (.d(hexdisplay_1_d2), .dp(hexdisplay_1_p2));
  Seven_Seg_Hex seven_seg_hex_2 (.d(hexdisplay_1_d1), .dp(hexdisplay_1_p1));
  hexdisplay hexdisplay_1 (
    .D1(hexdisplay_1_d1), .P1(hexdisplay_1_p1), .D2(hexdisplay_1_d2), .P2(hexdisplay_1_p2),
    .D3(hexdisplay_1_d3), .P3(hexdisplay_1_p3), .D4(hexdisplay_1_d4), .P4(hexdisplay_1_p4),
    .D5(hexdisplay_1_d5), .P5(hexdisplay_1_p5), .D6(hexdisplay_1_d6), .P6(hexdisplay_1_p6),
    .D7(hexdisplay_1_d7), .P7(hexdisplay_1_p7), .D8(hexdisplay_1_d8), .P8(hexdisplay_1_p8),
    .V({{16{1'b0}}, L_decimal}));
  fetch16 fetch16_1 (
    .instr(Program_d), .C(advance_out), .value(R_decimal), .jump(jmp), .pc(pc), .D_instr(fetch16_1_d_instr));
  Seven_Seg_Hex seven_seg_hex_3 (.d(hexdisplay_1_d3), .dp(hexdisplay_1_p3));
  Seven_Seg_Hex seven_seg_hex_4 (.d(hexdisplay_1_d4), .dp(hexdisplay_1_p4));
  Seven_Seg_Hex seven_seg_hex_5 (.d(hexdisplay_1_d5), .dp(hexdisplay_1_p5));
  Seven_Seg_Hex seven_seg_hex_6 (.d(hexdisplay_1_d6), .dp(hexdisplay_1_p6));
  Seven_Seg_Hex seven_seg_hex_7 (.d(hexdisplay_1_d7), .dp(hexdisplay_1_p7));
  Seven_Seg_Hex seven_seg_hex_8 (.d(hexdisplay_1_d8), .dp(hexdisplay_1_p8));
  decoder16 decoder16_1 (
    .D_inst(fetch16_1_d_instr), .L_in(L_rs), .R_in(R_rd), .rs(rs), .rd(rd), .L_out(L_decimal),
    .R_out(R_decimal), .mux_out(decoder16_1_mux_out), .add(add), .jump(jmp), .move(move), .op(op), .R_R(r_r));
  SixteenSeg sixteenseg_3 (.led(instdisplay_1_d1), .dp(instdisplay_1_p1));
  SixteenSeg sixteenseg_4 (.led(instdisplay_1_d2), .dp(instdisplay_1_p2));
  instdisplay instdisplay_1 (
    .D1(instdisplay_1_d1), .P1(instdisplay_1_p1), .D2(instdisplay_1_d2), .P2(instdisplay_1_p2),
    .D3(instdisplay_1_d3), .P3(instdisplay_1_p3), .D4(instdisplay_1_d4), .P4(instdisplay_1_p4),
    .D5(instdisplay_1_d5), .P5(instdisplay_1_p5), .D6(instdisplay_1_d6), .P6(instdisplay_1_p6), .I(op));
  SixteenSeg sixteenseg_5 (.led(instdisplay_1_d3), .dp(instdisplay_1_p3));
  SixteenSeg sixteenseg_6 (.led(instdisplay_1_d4), .dp(instdisplay_1_p4));
  SixteenSeg sixteenseg_7 (.led(instdisplay_1_d5), .dp(instdisplay_1_p5));
  SixteenSeg sixteenseg_8 (.led(instdisplay_1_d6), .dp(instdisplay_1_p6));
  exec16 exec16_1 (.L(L_decimal), .R(R_decimal), .mux_out(decoder16_1_mux_out), .sum(exec16_1_sum));
  Seven_Seg_Hex seven_seg_hex_9 (.d(hexdisplay_2_d2), .dp(hexdisplay_2_p2));
  Seven_Seg_Hex seven_seg_hex_10 (.d(hexdisplay_2_d1), .dp(hexdisplay_2_p1));
  hexdisplay hexdisplay_2 (
    .D1(hexdisplay_2_d1), .P1(hexdisplay_2_p1), .D2(hexdisplay_2_d2), .P2(hexdisplay_2_p2),
    .D3(hexdisplay_2_d3), .P3(hexdisplay_2_p3), .D4(hexdisplay_2_d4), .P4(hexdisplay_2_p4),
    .D5(hexdisplay_2_d5), .P5(hexdisplay_2_p5), .D6(hexdisplay_2_d6), .P6(hexdisplay_2_p6),
    .D7(hexdisplay_2_d7), .P7(hexdisplay_2_p7), .D8(hexdisplay_2_d8), .P8(hexdisplay_2_p8),
    .V({{16{1'b0}}, R_decimal}));
  Seven_Seg_Hex seven_seg_hex_11 (.d(hexdisplay_2_d3), .dp(hexdisplay_2_p3));
  Seven_Seg_Hex seven_seg_hex_12 (.d(hexdisplay_2_d4), .dp(hexdisplay_2_p4));
  Seven_Seg_Hex seven_seg_hex_13 (.d(hexdisplay_2_d5), .dp(hexdisplay_2_p5));
  Seven_Seg_Hex seven_seg_hex_14 (.d(hexdisplay_2_d6), .dp(hexdisplay_2_p6));
  regfile regfile_1 (
    .rs(rs), .rd(rd), .D(exec16_1_sum), .CL(advance_out), .R0(R0), .R1(R1), .R2(R2), .R3(R3), .L(L_rs),
    .R(R_rd));
  Seven_Seg_Hex seven_seg_hex_15 (.d(hexdisplay_2_d7), .dp(hexdisplay_2_p7));
  Seven_Seg_Hex seven_seg_hex_16 (.d(hexdisplay_2_d8), .dp(hexdisplay_2_p8));
  SixteenSeg sixteenseg_9 (.led(regdisplay_2_d1), .dp(regdisplay_2_p1));
  regdisplay regdisplay_2 (
    .D1(regdisplay_2_d1), .P1(regdisplay_2_p1), .D2(regdisplay_2_d2), .P2(regdisplay_2_p2), .E(r_r), .J(jmp),
    .R(rs));
  SixteenSeg sixteenseg_10 (.led(regdisplay_2_d2), .dp(regdisplay_2_p2));

  // Other names for the same wires on the sheet: L[15:0] = L_decimal; R[15:0] = R_decimal

  // Notes on the sheet:
  //   Fibonacci
  //   0: R2 = R2 + 1
  //   1: R2 = R2 + R1
  //   2: R3 = R2
  //   3: R1 = R1 + R2
  //   4: R3 = R1
  //   5: jump 1
  //   contents of Program (hex, n*v repeats v):
  //   120,61,bd,91,7d,10e
endmodule
